// Logisim project ctrl saut.circ as structural Verilog: 1 circuit, main circuit main
module main (
  input  [3:0] opcode,
  input  [3:0] flags,
  output [1:0] nextPCselect
);

  wire and_1_out, and_2_out, and_3_out, and_4_out, and_5_out, and_6_out, and_7_out, and_8_out;
  wire [1:1] bge, bgt, ble, blt, bne;

  not not_1 (bne[1], flags[2]);
  and and_1 (and_1_out, flags[1], flags[0]);
  and and_2 (and_2_out, ~flags[1], ~flags[0]);  // AND_Gate
  and and_3 (and_3_out, ~flags[1], flags[0]);  // AND_Gate
  and and_4 (and_4_out, flags[1], ~flags[0]);  // AND_Gate
  and and_5 (and_5_out, ~flags[2], ~flags[1], ~flags[0]);  // AND_Gate
  and and_6 (and_6_out, ~flags[2], flags[1], flags[0]);  // AND_Gate
  and and_7 (and_7_out, flags[1], ~flags[0]);  // AND_Gate
  and and_8 (and_8_out, ~flags[1], flags[0]);  // AND_Gate
  or or_1 (bge[1], and_1_out, and_2_out);
  or or_2 (ble[1], and_3_out, flags[2], and_4_out);
  or or_3 (bgt[1], and_5_out, and_6_out);
  or or_4 (blt[1], and_7_out, and_8_out);
  Multiplexer #(.select(4), .width(2)) multiplexer_1 (
    .in0(2'b00), .in1(2'b00), .in2(2'b00), .in3(2'b00), .in4(2'b00), .in5(2'b00), .in6(2'b00), .in7(2'b00),
    .in8(2'b01), .in9(2'b10), .in10({flags[2], 1'b0}), .in11({bne[1], 1'b0}), .in12({bge[1], 1'b0}),
    .in13({ble[1], 1'b0}), .in14({bgt[1], 1'b0}), .in15({blt[1], 1'b0}), .out(nextPCselect), .sel(opcode));  // open: en

  // Other names for the same wires on the sheet: OF = flags[0]; SF = flags[1]; beq[1] = flags[2]; ZF = flags[2];
  //   CF = flags[3]

  // Notes on the sheet:
  //   beq
  //   bne
  //   bge
  //   ble
  //   bgt
  //   blt
endmodule
